// Logisim project aiAlu.circ as structural Verilog: 7 circuits, main circuit Half Adder
module Half_Adder (
  input  a,
  input  b,
  output S,
  output c
);

  xor xor_1 (S, a, b);
  and and_1 (c, a, b);
endmodule

module Full_Adder (
  input  C0,
  input  a,
  input  b,
  output S,
  output c
);

  wire and_1_out, and_2_out, and_3_out, xor_1_out;

  xor xor_1 (xor_1_out, a, b);
  and and_1 (and_1_out, C0, a);
  and and_2 (and_2_out, C0, b);
  and and_3 (and_3_out, a, b);
  xor xor_2 (S, xor_1_out, C0);
  or or_1 (c, and_1_out, and_2_out, and_3_out);
endmodule

module Circuito_4_Bit (
  input  a3,
  input  a2,
  input  a1,
  input  a0,
  input  b3,
  input  b2,
  input  b1,
  input  b0,
  output cout,
  output s3,
  output s2,
  output s1,
  output s0
);

  wire full_adder_2_c, full_adder_3_c, half_adder_1_c;

  Full_Adder full_adder_1 (.S(s3), .c(cout), .C0(full_adder_2_c), .a(a3), .b(b3));
  Full_Adder full_adder_2 (.S(s2), .c(full_adder_2_c), .C0(full_adder_3_c), .a(a2), .b(b2));
  Full_Adder full_adder_3 (.S(s1), .c(full_adder_3_c), .C0(half_adder_1_c), .a(a1), .b(b1));
  Half_Adder half_adder_1 (.S(s0), .c(half_adder_1_c), .a(b0), .b(a0));
endmodule

module sommatore_4_bit (
  input  in_1,
  input  in_2,
  input  in_3,
  input  in_4,
  input  in_5,
  input  in_6,
  input  in_7,
  input  in_8,
  output out_9,
  output out_10,
  output out_11,
  output out_12,
  output out_13
);

  Circuito_4_Bit circuito_4_bit_1 (
    .a3(in_1), .a2(in_2), .a1(in_3), .a0(in_4), .b3(in_5), .b2(in_6), .b1(in_7), .b0(in_8), .cout(out_9),
    .s3(out_10), .s2(out_11), .s1(out_12), .s0(out_13));
endmodule

module circuito_8_bit (
  input  cin,
  input  a3,
  input  a2,
  input  a1,
  input  a0,
  input  b3,
  input  b2,
  input  b1,
  input  b0,
  output out_10,
  output out_11,
  output out_12,
  output out_13,
  output out_14
);

  wire full_adder_2_c, full_adder_3_c, full_adder_4_c;

  Full_Adder full_adder_1 (.S(out_11), .c(out_10), .C0(full_adder_2_c), .a(a3), .b(b3));
  Full_Adder full_adder_2 (.S(out_12), .c(full_adder_2_c), .C0(full_adder_3_c), .a(a2), .b(b2));
  Full_Adder full_adder_3 (.S(out_13), .c(full_adder_3_c), .C0(full_adder_4_c), .a(a1), .b(b1));
  Full_Adder full_adder_4 (.S(out_14), .c(full_adder_4_c), .C0(cin), .a(a0), .b(b0));
endmodule

module sommatore_8_bit (
  input  in_1,
  input  in_2,
  input  in_3,
  input  in_4,
  input  in_5,
  input  in_6,
  input  in_7,
  input  in_8,
  input  in_9,
  input  in_10,
  input  in_11,
  input  in_12,
  input  in_13,
  input  in_14,
  input  in_15,
  input  in_16,
  output out_17,
  output out_18,
  output out_19,
  output out_20,
  output out_21,
  output out_22,
  output out_23,
  output out_24,
  output out_25
);

  wire circuito_4_bit_1_cout;

  LED led_1 (.in(out_17));
  circuito_8_bit circuito_8_bit_1 (
    .a3(in_9), .a2(in_10), .a1(in_11), .a0(in_12), .b3(in_13), .b2(in_14), .b1(in_15), .b0(in_16),
    .cin(circuito_4_bit_1_cout), .out_10(out_17), .out_11(out_18), .out_12(out_19), .out_13(out_20),
    .out_14(out_21));
  Circuito_4_Bit circuito_4_bit_1 (
    .a3(in_1), .a2(in_2), .a1(in_3), .a0(in_4), .b3(in_5), .b2(in_6), .b1(in_7), .b0(in_8),
    .cout(circuito_4_bit_1_cout), .s3(out_22), .s2(out_23), .s1(out_24), .s0(out_25));
endmodule

module circuito_sommatorio_FINITO (
  input  [7:0] in_1,
  input  [7:0] in_2
);

  wire and_2_out, and_3_out, and_4_out, and_5_out, and_6_out, and_7_out, and_8_out;
  wire [0:0] and_1_out;

  and and_1 (and_1_out[0], in_1[0], in_2[0]);
  and and_2 (and_2_out, in_1[1], in_2[1]);
  and and_3 (and_3_out, in_1[2], in_2[2]);
  and and_4 (and_4_out, in_1[3], in_2[3]);
  and and_5 (and_5_out, in_1[4], in_2[4]);
  and and_6 (and_6_out, in_1[5], in_2[5]);
  and and_7 (and_7_out, in_1[6], in_2[6]);
  and and_8 (and_8_out, in_1[7], in_2[7]);
endmodule
